# Fritzing sketch PCB (saved by Fritzing 0.9.3b)
perfboards: 1

parts:
  Componente2 = Arduino Nano (Rev3.0)
  Componente3 = Motor Driver 1A Dual TB6612FNG
  S1 = SPST Switch [package=switch-spdt]
  S2 = Toggle Switch [package=THT]
  J1 = Screw terminal - 2 pins [package=THT]
  J2 = female pin header, 2 pins [form="♀ (female)"]
  J3 = female pin header, 2 pins [form="♀ (female)"]  # not connected
  J4 = female pin header, 2 pins [form="♀ (female)"]
  J5 = female pin header, 2 pins [form="♀ (female)"]
  J6 = female pin header, 2 pins [form="♀ (female)"]
  J7 = female pin header, 2 pins [form="♀ (female)"]
  J8 = female pin header, 2 pins [form="♀ (female)"]
  J9 = female pin header, 2 pins [form="♀ (female)"]  # not connected
  J10 = female pin header, 2 pins [form="♀ (female)"]  # not connected
  J11 = female pin header, 2 pins [form="♀ (female)"]
  J12 = female pin header, 2 pins [form="♀ (female)"]  # not connected
  J13 = female pin header, 2 pins [form="♀ (female)"]  # not connected
  J14 = female pin header, 2 pins [form="♀ (female)"]
  J15 = female pin header, 2 pins [form="♀ (female)"]
  J16 = female pin header, 2 pins [form="♀ (female)"]  # not connected
  J17 = female pin header, 2 pins [form="♀ (female)"]  # not connected
  J18 = female pin header, 2 pins [form="♀ (female)"]
  J19 = female pin header, 2 pins [form="♀ (female)"]  # not connected
  J20 = female pin header, 2 pins [form="♀ (female)"]  # not connected
  J21 = female pin header, 2 pins [form="♀ (female)"]  # not connected
  J22 = female pin header, 2 pins [form="♀ (female)"]  # not connected
  J23 = female pin header, 2 pins [form="♀ (female)"]
  J24 = female pin header, 2 pins [form="♀ (female)"]  # not connected
  J25 = female pin header, 2 pins [form="♀ (female)"]  # not connected
  J26 = female pin header, 2 pins [form="♀ (female)"]  # not connected
  J27 = female pin header, 2 pins [form="♀ (female)"]  # not connected
  J28 = female pin header, 2 pins [form="♀ (female)"]
  J29 = female pin header, 2 pins [form="♀ (female)"]  # not connected
  J32 = female pin header, 2 pins [form="♀ (female)"]
  J34 = Screw terminal - 2 pins [package=THT]
  J35 = Screw terminal - 2 pins [package=THT]
  J36 = female pin header, 2 pins [form="♀ (female)"]
  J37 = female pin header, 2 pins [form="♀ (female)"]
  J38 = female pin header, 2 pins [form="♀ (female)"]
  J39 = female pin header, 2 pins [form="♀ (female)"]
  J40 = female pin header, 2 pins [form="♀ (female)"]
  S3 = Toggle Switch [package=THT]
  L1 = Solenoid
  L2 = Solenoid
  VCC1 = Battery block 9V

nets:
  N1: Componente2.GND, J39.pin1
  N2: Componente2.VIN, S1.O
  N3: Componente2.3V3, J28.pin1
  N4: Componente3.VCC, J23.pin2
  N5: Componente3.PWMA, J18.pin2
  N6: Componente3.AIN2, J11.pin1
  N7: Componente3.AIN1, J11.pin2
  N8: Componente3.STBY, J14.pin1
  N9: Componente3.BIN1, J14.pin2
  N10: Componente3.BIN2, J15.pin1
  N11: Componente3.PWMB, J15.pin2
  N12: S1.P, J32.pin2
  N13: S2.L1, J2.pin1
  N14: S2.COM, J7.pin2
  N15: S2.L2, J37.pin1
  N16: J1.pin1, VCC1.+
  N17: J1.pin2, VCC1.-
  N18: J2.pin2, S3.L2
  N19: J4.pin1, J8.pin2, J36.pin2, J40.pin1
  N20: J5.pin1, J38.pin2
  N21: J5.pin2, J36.pin1
  N22: J6.pin1, S3.COM
  N23: J6.pin2, J38.pin1
  N24: J7.pin1, J40.pin2
  N25: J34.pin1, L1.pin2
  N26: J34.pin2, L1.pin1
  N27: J35.pin1, L2.pin2
  N28: J35.pin2, L2.pin1
  N29: J37.pin2, S3.L1

notes:
  *rojo-7.4V batería
  *naranja- 5V
  *amarillo- 3.3V
  *negro- GND
  *rosa-pines siguelíneas que dos de ellos tienen la posibilidad de conmutarse para usarse para i2c
  *conexiones driver-arduino ya soldadas
  *todos los cables irían por detrás de la placa
